# Fritzing sketch PCB (saved by Fritzing 0.9.0b)
circuit board: 14.7cm x 8.8cm
breadboards: 1

parts:
  U1 = XBee
  Part2 = Arduino Mega 2560 (Rev3)
  Part3 = OpenLog
  IMU1 = Adafruit 10-DOF IMU Breakout

nets:
  VCC: U1.VCC, U1.pin2, Part2.3V3, Part2.D0_RX0, Part3.VCC, IMU1.3Vo
  N1: U1.pin3, Part2.D1_TX0
  N2: U1.pin5, U1.pin6, U1.pin7, U1.pin8, U1.pin9
  GND: U1.GND, Part2.GND, Part3.GND, IMU1.GND
  N3: U1.pin12, U1.pin13, U1.pin14, U1.pin15, U1.pin16
  N4: U1.pin19, U1.pin20
  N5: Part2.D21/SCL, IMU1.SCL
  N6: Part2.D20/SDA, IMU1.SDA
  N7: Part2.D17_PWM/RX2, Part3.TXO
  N8: Part2.D16_PWM/TX2, Part3.RXI
