# Fritzing sketch PCB (saved by Fritzing 0.9.0b)
breadboards: 1

parts:
  U1 = XBee
  Part1 = Arduino Mega ADK (Rev3)

nets:
  VCC: U1.VCC, U1.pin2, U1.pin3, Part1.3V3, Part1.D0/RX0, Part1.D1/TX0
  GND: U1.pin6, U1.pin7, U1.pin8, U1.pin9, U1.GND, Part1.GND
  N1: U1.pin11, U1.pin12, U1.pin13, U1.pin14, U1.pin15
  N2: U1.pin18, U1.pin19, U1.pin20
